# Fritzing sketch main_wireing (saved by Fritzing 0.9.4)

parts:
  U1 = ESP32S-HiLetgo [part_number=ESP32S-HiLetgo]
  OLED_I2C1 = OLED 128x64 I2C Monochrome Display
  microSD1 = MicroSD Card Module

nets:
  VDD: U1.3.3, OLED_I2C1.VDD, microSD1.VCC
  N1: U1.GPIO5, microSD1.CS
  N2: U1.GPIO18, microSD1.SCK
  N3: U1.GPIO19, microSD1.MISO
  GND: U1.GND, OLED_I2C1.GND, microSD1.GND
  N4: U1.GPIO21, OLED_I2C1.SDA
  N5: U1.GPIO22, OLED_I2C1.SCK
  N6: U1.GPIO23, microSD1.MOSI

custom parts:
  ESP32S-HiLetgo: HiLetgo ESP-WROOM-32 ESP32 ESP-32S Development Board 2.4GHz Dual-Mode WiFi + Bluetooth Dual Cores Microcontroller The ESP32 integrated with Antenna switches, RF Balun, power amplifiers, low-noise amplifiers, filters, and management modules, and the entire solution occupies the least area of PCB. 2.4 GHz Wi-Fi plus Bluetooth dual-mode chip, with TSMC Ultra-low power consumption 40nm technology,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
